# Fritzing sketch oleTSW_Controller-v0.1 (saved by Fritzing 1.0.4)
breadboards: 1

parts:
  MCU1 = Wemos Lolin32lite
  U3 = SLIDER [knob_status=50% power=0.5W package=slider]
  U5 = SLIDER [knob_status=50% power=0.5W package=slider]
  C1 = Ceramic Capacitor [capacitance=100nF voltage=35V package="100 mil [THT, multilayer]"]
  C2 = Ceramic Capacitor [capacitance=100nF voltage=35V package="100 mil [THT, multilayer]"]
  C3 = Ceramic Capacitor [capacitance=100nF voltage=35V package="100 mil [THT, multilayer]"]
  U6 = SLIDER [knob_status=50% power=0.5W package=slider]
  U7 = MCP23S17 I2C I/O Expander
  U8 = MCP23S17 I2C I/O Expander

nets:
  N1: MCU1.pin_4, U5.S, C3.1
  N2: MCU1.pin_6, U3.S, C1.1
  N3: MCU1.pin_13, U3.A, U5.A, C1.0, C2.0, C3.0, U6.A
  N4: MCU1.pin_23, U7.CS, U8.CS
  N5: MCU1.pin_24, U7.SCK, U8.SCK
  N6: MCU1.pin_25, U7.SI, U8.SI
  N7: MCU1.pin_26, U7.SO, U8.SO
  N8: MCU1.pin_28, U3.E, U5.E, U6.E
  N9: C2.1, U6.S
  VDD: U7.VDD, U7.A0, U8.VDD
  VSS: U7.VSS, U7.A1, U7.A2, U8.VSS, U8.A0, U8.A1, U8.A2

custom parts:
  Wemos Lolin32lite: Wemos Lolinlite32 wifi and blue tooth board based on the ESP-32 cpu, digital I/Os 19, analog inputs 6, clock 240mhz, Flash 4Mbytes, lipo battery charger (500ma connection broken out on breadboard but not pcb), usb.
  MCP23S17 I2C I/O Expander: The MCP23S17 uses fourspi pins , and in exchange gives you 16 general purpose pins. You can set each of 16 pins to be input, output, input with a pullup or open drain. There's even the ability to get an interrupt via an external pin when any of the inputs change so you don't have to keep polling the chip.
